# Fritzing sketch polaroid (saved by Fritzing 0.9.0b)
breadboards: 1

parts:
  R1 = Resistor [tolerance=±5% resistance=10k package=THT]
  R2 = Resistor [tolerance=±5% resistance=10k package=THT]
  LED1 = LED - 5mm [color="Red (633nm)" package="5 mm [THT]"]
  R3 = Resistor [tolerance=±5% resistance=10k package=THT]
  S1 = Pushbutton [package=THT]
  S2 = Pushbutton [package=THT]
  Raspberry_Pi1 = Raspberry Pi B rev2

nets:
  N1: R1.Pin_0, R2.Pin_0, Raspberry_Pi1.5V
  N2: R1.Pin_1, S1.leg1, Raspberry_Pi1.GPIO_24
  N3: R2.Pin_1, S2.leg1, Raspberry_Pi1.GPIO_23
  N4: LED1.cathode, R3.Pin_0
  N5: LED1.anode, Raspberry_Pi1.GPIO_18
  N6: R3.Pin_1, S1.leg0, S2.leg0, Raspberry_Pi1.GND
